// Logisim project NARCY.circ as structural Verilog: 2 circuits, main circuit main
module main (
);

  wire clk_GPR_A, clk_GPR_B, clk_GPR_C, clk_IR, clk_PC, clk_RAM_ADDR, clk_RAM_DATA, clock_1_out,
       decoder_1_out1, decoder_1_out2, decoder_1_out3, flg_GPR_A_ENBL, flg_GPR_A_WRITE, flg_GPR_B_ENBL,
       flg_GPR_B_WRITE, flg_GPR_C_ENBL, flg_GPR_C_WRITE, flg_IR_WRITE, flg_PC_ENBL, flg_RAM_ADDR_HI_WRITE,
       flg_RAM_ADDR_LO_WRITE, flg_RAM_ENBL, flg_RAM_WRITE, inc_PC, or_1_out, rst_PC;
  wire [1:0] counter_1_q;
  wire [7:0] AR_HI_q, AR_LO_q, DATA_BUS, GPR_A_q, GPR_B_q, GPR_C_q, IR_q, PC_q, ram_1_dout,
       registerreadwriteprotection_1_registerin, registerreadwriteprotection_2_registerin,
       registerreadwriteprotection_3_registerin, registerreadwriteprotection_4_registerin,
       registerreadwriteprotection_5_dout, registerreadwriteprotection_5_registerin,
       registerreadwriteprotection_6_dout, registerreadwriteprotection_6_registerin,
       registerreadwriteprotection_7_dout, registerreadwriteprotection_7_registerin;
  wire [63:0] rom_1_data;

  Register GPR_A (.D(registerreadwriteprotection_1_registerin), .Q(GPR_A_q), .clk(clk_GPR_A));  // open: en, clr
  RegisterReadWriteProtection registerreadwriteprotection_1 (
    .RegisterIn(registerreadwriteprotection_1_registerin), .Dout(DATA_BUS), .write(flg_GPR_A_WRITE),
    .Din(DATA_BUS), .RegisterOut(GPR_A_q), .enable(flg_GPR_A_ENBL));
  Register GPR_B (.D(registerreadwriteprotection_2_registerin), .Q(GPR_B_q), .clk(clk_GPR_B));  // open: en, clr
  RegisterReadWriteProtection registerreadwriteprotection_2 (
    .RegisterIn(registerreadwriteprotection_2_registerin), .Dout(DATA_BUS), .write(flg_GPR_B_WRITE),
    .Din(DATA_BUS), .RegisterOut(GPR_B_q), .enable(flg_GPR_B_ENBL));
  Register GPR_C (.D(registerreadwriteprotection_3_registerin), .Q(GPR_C_q), .clk(clk_GPR_C));  // open: en, clr
  RegisterReadWriteProtection registerreadwriteprotection_3 (
    .RegisterIn(registerreadwriteprotection_3_registerin), .Dout(DATA_BUS), .write(flg_GPR_C_WRITE),
    .Din(DATA_BUS), .RegisterOut(GPR_C_q), .enable(flg_GPR_C_ENBL));
  Counter PC (
    .D(registerreadwriteprotection_4_registerin), .Q(PC_q), .clk(inc_PC), .clr(rst_PC));  // open: load, count, carry, up
  RegisterReadWriteProtection registerreadwriteprotection_4 (
    .RegisterIn(registerreadwriteprotection_4_registerin), .Dout(DATA_BUS), .write(clk_PC), .Din(DATA_BUS),
    .RegisterOut(PC_q), .enable(flg_PC_ENBL));
  Register AR_HI (.D(registerreadwriteprotection_5_registerin), .Q(AR_HI_q), .clk(clk_RAM_ADDR));  // open: en, clr
  RegisterReadWriteProtection registerreadwriteprotection_5 (
    .RegisterIn(registerreadwriteprotection_5_registerin), .Dout(registerreadwriteprotection_5_dout),
    .write(flg_RAM_ADDR_HI_WRITE), .Din(DATA_BUS), .RegisterOut(AR_HI_q), .enable(1'b1));
  Register AR_LO (.D(registerreadwriteprotection_6_registerin), .Q(AR_LO_q), .clk(clk_RAM_ADDR));  // open: en, clr
  RegisterReadWriteProtection registerreadwriteprotection_6 (
    .RegisterIn(registerreadwriteprotection_6_registerin), .Dout(registerreadwriteprotection_6_dout),
    .write(flg_RAM_ADDR_LO_WRITE), .Din(DATA_BUS), .RegisterOut(AR_LO_q), .enable(1'b1));
  // Probe on DATA_BUS
  // Probe on {registerreadwriteprotection_6_dout, registerreadwriteprotection_5_dout}
  RAM #(.addrWidth(16), .enables("line")) ram_1 (
    .addr({registerreadwriteprotection_6_dout, registerreadwriteprotection_5_dout}), .we(flg_RAM_WRITE),
    .clk(clk_RAM_DATA), .din(DATA_BUS), .dout(ram_1_dout));
  Register IR (.D(registerreadwriteprotection_7_registerin), .Q(IR_q), .clk(clk_IR));  // open: en, clr
  RegisterReadWriteProtection registerreadwriteprotection_7 (
    .RegisterIn(registerreadwriteprotection_7_registerin), .Dout(registerreadwriteprotection_7_dout),
    .write(flg_IR_WRITE), .Din(DATA_BUS), .RegisterOut(IR_q), .enable(1'b1));
  ROM #(.dataWidth(64)) rom_1 (.addr(registerreadwriteprotection_7_dout), .data(rom_1_data));
  assign DATA_BUS = flg_RAM_ENBL ? ram_1_dout : 8'bz;  // Controlled_Buffer controlled_buffer_1
  Clock clock_1 (.out(clock_1_out));
  Decoder #(.select(2)) decoder_1 (
    .out1(decoder_1_out1), .out2(decoder_1_out2), .out3(decoder_1_out3), .sel(counter_1_q));  // open: out0, en
  Counter #(.max('h3), .width(2)) counter_1 (
    .Q(counter_1_q), .clk(clock_1_out));  // open: load, D, count, carry, up, clr
  assign {clk_GPR_C, clk_GPR_B, clk_GPR_A, clk_RAM_DATA, clk_RAM_ADDR, clk_PC, clk_IR} = decoder_1_out3 ? rom_1_data[6:0] : 7'bz;  // Controlled_Buffer controlled_buffer_2
  or or_1 (or_1_out, decoder_1_out3, decoder_1_out2);
  assign {flg_GPR_C_ENBL, flg_GPR_B_ENBL, flg_GPR_A_ENBL, flg_RAM_ENBL, flg_PC_ENBL, flg_GPR_C_WRITE, flg_GPR_B_WRITE, flg_GPR_A_WRITE, flg_RAM_WRITE, flg_RAM_ADDR_LO_WRITE, flg_RAM_ADDR_HI_WRITE, flg_IR_WRITE} = or_1_out ? rom_1_data[27:16] : 12'bz;  // Controlled_Buffer controlled_buffer_3
  assign {rst_PC, inc_PC} = decoder_1_out1 ? rom_1_data[33:32] : 2'bz;  // Controlled_Buffer controlled_buffer_4
  Pull_Resistor pull_resistor_1 (.node({clk_GPR_C, clk_GPR_B, clk_GPR_A, clk_RAM_DATA, clk_RAM_ADDR, clk_PC, clk_IR}));
  Pull_Resistor pull_resistor_2 (.node({flg_GPR_C_ENBL, flg_GPR_B_ENBL, flg_GPR_A_ENBL, flg_RAM_ENBL, flg_PC_ENBL, flg_GPR_C_WRITE, flg_GPR_B_WRITE, flg_GPR_A_WRITE, flg_RAM_WRITE, flg_RAM_ADDR_LO_WRITE, flg_RAM_ADDR_HI_WRITE, flg_IR_WRITE}));
  Pull_Resistor pull_resistor_3 (.node({rst_PC, inc_PC}));

  // Notes on the sheet:
  //   contents of rom_1 (hex, n*v repeats v):
  //   100810001
endmodule

module RegisterReadWriteProtection (
  input  [7:0] RegisterOut,
  input  write,
  input  enable,
  input  [7:0] Din,
  output [7:0] Dout,
  output [7:0] RegisterIn
);

  wire not_1_out;

  not not_1 (not_1_out, write);
  assign RegisterIn = not_1_out ? RegisterOut : 8'bz;  // Controlled_Buffer controlled_buffer_1
  assign RegisterIn = write ? Din : 8'bz;  // Controlled_Buffer controlled_buffer_2
  assign Dout = enable ? RegisterOut : 8'bz;  // Controlled_Buffer controlled_buffer_3

  // Notes on the sheet:
  //   write: pull=down
endmodule
